# Fritzing sketch schematic (saved by Fritzing 0.9.3b)
breadboards: 1

parts:
  U1 = NodeMCU V1.0
  Part1 = Logic Level Converter
  Power_plug1 = Power plug
  U2 = Mini-360 DC-DC Buck converter [package=THT]
  U3 = Hirose DF13 Series Header [part_number=DF13#-3P-1.25V package=DF13C-3P-1.25V]

nets:
  N1: U1.D1, Part1.TX_LV
  N2: U1.3V3, Part1.LV
  GND: U1.GND, Part1.HV, Part1.GND, Power_plug1.GND, U2.IN-, U2.OUT-, U3.3
  N3: U1.Vin, U2.OUT+
  N4: Part1.TX_HV, U3.2
  N5: Power_plug1.VCC, U2.IN+, U3.1

notes:
  12V
  Data
  GND
  RGB LED Strip Connector

custom parts:
  NodeMCU V1.0: ESP8266 based NodeMCU
  Mini-360 DC-DC Buck converter: Mini-360 DC-DC Buck converter. Tiny buck step down voltage converter, input voltage 4.75 to 23V output 1 to 17V adjustable. Available from ebay and the like.
